// Logisim project skyarch-cpu.circ as structural Verilog: 36 circuits, main circuit micronme
module micronme (
  input  Clock,
  input  [5:0] IRQ,
  input  [2:0] EX,
  input  BA,
  input  LOCK,
  input  [3:0] COB,
  input  Reset,
  input  [3:0] COP,
  output [1:0] Status,
  output W,
  output IO,
  output SC,
  output CX,
  output [29:0] Addr,
  output [3:0] COE
);

  wire BE_p1, BE_p3, busmaster_avail, CU_busen, CU_busreset, CU_cx, CU_io, CU_sc, CU_w, decoder_1_out1;
  wire [31:0] busmaster_dataoutput, busmaster_readout, CU_addr, CU_wdata, Data_p4;

  // PortIO #(.number(1)) BE: pin names not known; wires that end beside it: BE_p1, BE_p1, BE_p3
  controlunit CU (
    .RESET(Reset), .COB(COB), .clk(Clock), .RData(busmaster_readout), .BusAvail(busmaster_avail), .IRQ(IRQ),
    .EX(EX), .BusReset(CU_busreset), .WData(CU_wdata), .Addr(CU_addr), .SC(CU_sc), .W(CU_w), .IO(CU_io),
    .BusEN(CU_busen), .status(Status), .CX(CU_cx));  // open: clkout
  busmanager busmaster (
    .SCIn(CU_sc), .WIn(CU_w), .IOIn(CU_io), .BusEN(CU_busen), .Ain(CU_addr), .ExBE(BE_p3), .DIn(CU_wdata),
    .Clock(Clock), .Reset(CU_busreset), .datain(Data_p4), .LOCK(LOCK), .CXIn(CU_cx), .ACk(BA),
    .Avail(busmaster_avail), .BE(BE_p1), .readout(busmaster_readout), .W(W), .IO(IO), .SC(SC), .AOut(Addr),
    .dataoutput(busmaster_dataoutput), .CX(CX));  // open: sz
  Decoder decoder_1 (.out1(decoder_1_out1), .sel(W), .en(BE_p1));  // open: out0
  // PortIO #(.number(32)) Data: pin names not known; wires that end beside it: 1'b0, decoder_1_out1, busmaster_dataoutput, Data_p4
endmodule

module regmap (
  input  [31:0] writeval,
  input  [4:0] readregno,
  input  [31:0] gprr0,
  input  [4:0] addrregno,
  input  [31:0] ioread,
  input  [4:0] writeregno,
  input  [3:0] mapno,
  input  [31:0] sysctlread,
  input  wb,
  input  dir,
  input  write,
  input  [31:0] gprr1,
  input  shift,
  input  [7:0] portno,
  input  [4:0] width,
  input  clock,
  input  [31:0] rdata,
  input  busavail,
  output [4:0] rregno,
  output gpr1read,
  output [4:0] gpr1regno,
  output [31:0] rval,
  output [4:0] wregno,
  output error,
  output [31:0] wval,
  output gprwrite,
  output iowrite,
  output syswrite,
  output shiften,
  output [4:0] swidth,
  output be,
  output w,
  output io,
  output sc,
  output [31:0] addr,
  output [31:0] wdata
);

  wire bitselector_1_out, demultiplexer_1_out0, demultiplexer_1_out1, demultiplexer_1_out3, not_1_out,
       not_2_out, or_1_out;
  wire [3:3] and_2_out;
  wire [4:0] multiplexer_7_out;
  wire [31:0] multiplexer_4_out, regvalidrom_data;

  and and_1 (gpr1read, addrregno[0], addrregno[1], addrregno[2], addrregno[3], addrregno[4]);
  Multiplexer multiplexer_1 (.in0(write), .in1(demultiplexer_1_out0), .out(gprwrite), .sel(dir));
  Multiplexer multiplexer_2 (.in0(1'b0), .in1(demultiplexer_1_out3), .out(iowrite), .sel(dir));
  Multiplexer multiplexer_3 (.in0(1'b0), .in1(demultiplexer_1_out1), .out(syswrite), .sel(dir));
  Multiplexer #(.enable("true"), .select(3), .width(32)) multiplexer_4 (
    .in0(gprr0), .in1(sysctlread), .in2({32{1'b0}}), .in3(ioread), .in4({32{1'b0}}), .in5({32{1'b0}}),
    .in6({32{1'b0}}), .in7({32{1'b0}}), .out(multiplexer_4_out), .sel(mapno[2:0]), .en(mapno[3]));
  Multiplexer #(.width(32)) multiplexer_5 (.in0(gprr0), .in1(multiplexer_4_out), .out(rval), .sel(not_1_out));
  not not_1 (not_1_out, dir);
  not not_2 (not_2_out, mapno[3]);
  or or_1 (or_1_out, write, error);
  Demultiplexer #(.enable("true"), .select(3)) demultiplexer_1 (
    .out0(demultiplexer_1_out0), .out1(demultiplexer_1_out1), .out3(demultiplexer_1_out3), .in(or_1_out),
    .sel(mapno[2:0]), .en(not_2_out));  // open: out2, out4, out5, out6, out7
  Multiplexer #(.width(32)) multiplexer_6 (.in0(writeval), .in1(rval), .out(wval), .sel(wb));
  Multiplexer #(.width(5)) multiplexer_7 (.in0(readregno), .in1(writeregno), .out(multiplexer_7_out), .sel(dir));
  and and_2 (and_2_out[3], dir, write);
  not not_3 (error, bitselector_1_out);
  BitSelector #(.width(32)) bitselector_1 (.in(regvalidrom_data), .out(bitselector_1_out), .sel(multiplexer_7_out));
  ROM #(.addrWidth(4), .dataWidth(32)) regvalidrom (.addr({and_2_out[3], mapno[2:0]}), .data(regvalidrom_data));

  assign gpr1regno = addrregno;
  assign rregno = readregno;
  assign shiften = shift;
  assign swidth = width;
  assign wregno = writeregno;

  // Notes on the sheet:
  //   contents of regvalidrom (hex, n*v repeats v):
  //   ffffffff 80000005 ffffffff ffffffff c00000ff 0 0 0 ffffffff 80000005 0 ffffffff c00000ff
endmodule

module sysconf (
  input  [4:0] regno,
  output [31:0] Data,
  output [29:0] itaddr
);
endmodule

module busmanager (
  input  SCIn,
  input  WIn,
  input  IOIn,
  input  BusEN,
  input  [31:0] Ain,
  input  ExBE,
  input  [31:0] DIn,
  input  Clock,
  input  [1:0] sz,
  input  Reset,
  input  [31:0] datain,
  input  LOCK,
  input  CXIn,
  input  ACk,
  output Avail,
  output BE,
  output [31:0] readout,
  output W,
  output IO,
  output SC,
  output [29:0] AOut,
  output [31:0] dataoutput,
  output CX
);

  wire and_2_out, and_3_out, and_4_out, and_5_out, and_6_out, and_7_out, controlled_buffer_1_out,
       controlled_buffer_2_out, controlled_buffer_5_out, counter_1_carry, counter_2_carry, d_ff_1_q,
       d_ff_2_q, decoder_1_out0, decoder_1_out1, decoder_1_out2, decoder_2_out0, decoder_3_out0,
       extavail_avail, IOBuf_q, multiplexer_1_out, multiplexer_2_out, not_1_out, not_2_out, or_1_out,
       or_2_out, or_3_out, or_4_out, or_5_out, or_6_out, or_7_out, or_8_out, or_9_out, or_10_out, s_r_ff_1_q,
       s_r_ff_1_qn, s_r_ff_2_q, s_r_ff_2_qn, s_r_ff_5_q, SCBuf_q, WBuf_q;
  wire [1:0] ABus_q, counter_1_q, SZBuf_q;
  wire [2:0] counter_2_q;
  wire [29:0] ABuf2_q, ABus_q_2;
  wire [31:0] DBuf2_q, DBus_q, register_2_q;

  and and_1 (Avail, s_r_ff_2_qn, s_r_ff_1_qn);
  S_R_Flip_Flop s_r_ff_1 (
    .S(CXIn), .clk(Clock), .Q(s_r_ff_1_q), .reset(or_5_out), .Qn(s_r_ff_1_qn));  // open: R, preset
  Register #(.width(1)) WBuf (.D(WIn), .en(BusEN), .clk(Clock), .Q(WBuf_q), .clr(or_5_out));
  S_R_Flip_Flop s_r_ff_2 (
    .S(BusEN), .clk(Clock), .Q(s_r_ff_2_q), .reset(or_5_out), .Qn(s_r_ff_2_qn));  // open: R, preset
  and and_2 (and_2_out, BusEN, WIn);
  Register #(.width(1)) SCBuf (.D(SCIn), .en(BusEN), .clk(Clock), .Q(SCBuf_q), .clr(or_5_out));
  Register #(.width(1)) IOBuf (.D(IOIn), .en(BusEN), .clk(Clock), .Q(IOBuf_q), .clr(or_5_out));
  or or_1 (or_1_out, WIn, s_r_ff_1_q);
  or or_2 (or_2_out, and_2_out, s_r_ff_1_q);
  Register #(.width(2)) SZBuf (.D(sz), .en(BusEN), .clk(Clock), .Q(SZBuf_q), .clr(or_5_out));
  Register #(.width(32)) ABus (.D(Ain), .en(or_1_out), .clk(Clock), .Q({ABus_q_2, ABus_q}), .clr(or_5_out));
  Register #(.width(32)) DBus (.D(DIn), .en(or_2_out), .clk(Clock), .Q(DBus_q), .clr(or_5_out));
  or or_3 (or_3_out, SCBuf_q, s_r_ff_1_q);
  or or_4 (or_4_out, IOBuf_q, s_r_ff_1_q);
  Register #(.width(32)) register_1 (.D(register_2_q), .en(d_ff_1_q), .Q(readout));  // open: clk, clr
  and and_3 (and_3_out, s_r_ff_2_q, extavail_avail);
  or or_5 (or_5_out, counter_1_carry, or_6_out);
  Decoder #(.select(2)) decoder_1 (
    .out0(decoder_1_out0), .out1(decoder_1_out1), .out2(decoder_1_out2), .sel(SZBuf_q), .en(s_r_ff_2_q));  // open: out3
  Counter #(.max('h3), .ongoal("stay"), .width(2)) counter_1 (
    .clr(not_1_out), .load(not_1_out), .up(s_r_ff_1_q), .count(s_r_ff_1_q), .clk(Clock),
    .carry(counter_1_carry), .Q(counter_1_q));  // open: D
  not not_1 (not_1_out, s_r_ff_1_q);
  or or_6 (or_6_out, Reset, multiplexer_2_out);
  not not_2 (not_2_out, and_3_out);
  Counter #(.max('h7), .ongoal("stay"), .width(3)) counter_2 (
    .clr(not_2_out), .load(not_2_out), .up(and_3_out), .count(and_3_out), .clk(Clock),
    .carry(counter_2_carry), .Q(counter_2_q));  // open: D
  Decoder #(.select(2)) decoder_2 (
    .out0(decoder_2_out0), .sel(counter_1_q), .en(s_r_ff_1_q));  // open: out1, out2, out3
  and and_4 (and_4_out, ACk, WBuf_q);
  Multiplexer multiplexer_1 (.in0(and_4_out), .in1(WBuf_q), .out(multiplexer_1_out), .sel(decoder_1_out2));
  or or_7 (or_7_out, counter_2_carry, and_5_out);
  buf and_5 (and_5_out, counter_2_q[2]);  // AND_Gate
  Register #(.trigger("falling"), .width(32)) DBuf2 (.D(DBus_q), .en(WBuf_q), .clk(Clock), .Q(DBuf2_q), .clr(or_5_out));
  Multiplexer multiplexer_2 (.in0(or_7_out), .in1(d_ff_2_q), .out(multiplexer_2_out), .sel(multiplexer_1_out));
  Decoder #(.select(2)) decoder_3 (
    .out0(decoder_3_out0), .sel(counter_2_q[1:0]), .en(and_3_out));  // open: out1, out2, out3
  D_Flip_Flop #(.trigger("falling")) d_ff_1 (
    .D(s_r_ff_5_q), .clk(Clock), .Q(d_ff_1_q), .reset(or_5_out));  // open: Qn, preset
  D_Flip_Flop #(.trigger("falling")) d_ff_2 (
    .D(d_ff_1_q), .clk(Clock), .Q(d_ff_2_q), .reset(or_5_out));  // open: Qn, preset
  S_R_Flip_Flop s_r_ff_3 (.S(decoder_3_out0), .clk(Clock), .Q(BE), .reset(or_5_out));  // open: R, Qn, preset
  S_R_Flip_Flop s_r_ff_4 (.S(decoder_2_out0), .clk(Clock), .Q(CX), .reset(or_5_out));  // open: R, Qn, preset
  busavail extavail (.BE(ExBE), .Lock(LOCK), .sc(or_3_out), .IO(or_4_out), .AVAIL(extavail_avail));
  or or_8 (or_8_out, and_7_out, s_r_ff_5_q);
  Register #(.trigger("falling"), .width(32)) register_2 (
    .D(datain), .en(or_9_out), .clk(Clock), .Q(register_2_q), .clr(or_5_out));
  or or_9 (or_9_out, or_8_out, CX);
  Register #(.trigger("falling"), .width(30)) ABuf2 (
    .D(ABus_q_2), .en(or_10_out), .clk(Clock), .Q(ABuf2_q), .clr(or_5_out));
  or or_10 (or_10_out, BE, CX);
  assign controlled_buffer_1_out = BE ? multiplexer_1_out : 1'bz;  // Controlled_Buffer controlled_buffer_1
  assign controlled_buffer_2_out = BE ? or_3_out : 1'bz;  // Controlled_Buffer controlled_buffer_2
  assign AOut = BE ? ABuf2_q : 30'bz;  // Controlled_Buffer controlled_buffer_3
  and and_6 (and_6_out, BE, multiplexer_1_out);
  assign dataoutput = and_6_out ? DBuf2_q : 32'bz;  // Controlled_Buffer controlled_buffer_4
  assign controlled_buffer_5_out = BE ? or_4_out : 1'bz;  // Controlled_Buffer controlled_buffer_5
  and and_7 (and_7_out, BE, multiplexer_1_out);
  Multiplexer multiplexer_3 (.in0(controlled_buffer_1_out), .in1(CX), .out(W), .sel(CX));
  S_R_Flip_Flop s_r_ff_5 (.S(ACk), .clk(Clock), .Q(s_r_ff_5_q), .reset(or_5_out));  // open: R, Qn, preset
  Multiplexer multiplexer_4 (.in0(controlled_buffer_5_out), .in1(CX), .out(IO), .sel(CX));
  Multiplexer multiplexer_5 (.in0(controlled_buffer_2_out), .in1(CX), .out(SC), .sel(CX));
endmodule

module busavail (
  input  BE,
  input  Lock,
  input  sc,
  input  IO,
  output AVAIL
);

  wire or_1_out;

  or or_1 (or_1_out, ~Lock, sc, IO);  // OR_Gate
  and and_1 (AVAIL, ~BE, or_1_out);  // AND_Gate
endmodule

module controlunit (
  input  RESET,
  input  [3:0] COB,
  input  clk,
  input  [31:0] RData,
  input  BusAvail,
  input  [5:0] IRQ,
  input  [2:0] EX,
  output BusReset,
  output [31:0] WData,
  output [31:0] Addr,
  output SC,
  output W,
  output IO,
  output BusEN,
  output [1:0] status,
  output clkout,
  output CX
);

  wire rdispatch_be, rdispatch_error, rdispatch_gpr1read, rdispatch_gprwrite, rdispatch_iowrite,
       rdispatch_sc, statuscu_p3, statuscu_p4, statuscu_p5, statuscu_p7;
  wire [4:0] multiplexer_3_out, multiplexer_4_out, rdispatch_gpr1regno, rdispatch_rregno, rdispatch_wregno;
  wire [31:0] gprlist_read0data, gprlist_read1data, iolist_readval, multiplexer_5_out, rdispatch_addr,
       rdispatch_rval, rdispatch_wdata, rdispatch_wval;

  and and_1 (clkout, clk, statuscu_p7);
  Multiplexer #(.enable("true"), .width(32)) multiplexer_1 (
    .in1(rdispatch_wdata), .out(WData), .sel(rdispatch_be), .en(BusEN));  // open: in0
  Multiplexer #(.enable("true"), .width(32)) multiplexer_2 (
    .in1(rdispatch_addr), .out(Addr), .sel(rdispatch_be), .en(BusEN));  // open: in0
  // statusunit statuscu: pin names not known; wires that end beside it: COB, clk, statuscu_p3, statuscu_p4, statuscu_p5, RESET, statuscu_p7, status
  ioregs iolist (
    .clock(clkout), .reset(RESET), .readreg(rdispatch_rregno), .wregno(multiplexer_3_out),
    .WE(rdispatch_iowrite), .writeval(multiplexer_5_out), .readval(iolist_readval));  // open: SE, width, portout
  gprs gprlist (
    .clock(clkout), .WData1(rdispatch_wval), .read0regno(rdispatch_rregno), .read1regno(multiplexer_4_out),
    .wregno1(rdispatch_wregno), .WE1(rdispatch_gprwrite), .Reset(RESET), .read0data(gprlist_read0data),
    .read1data(gprlist_read1data));  // open: read2regno, WData2, wregno2, WE2, read2data
  buf or_1 (BusEN, rdispatch_be);  // OR_Gate
  buf or_2 (SC, rdispatch_sc);  // OR_Gate
  regmap rdispatch (
    .gprr0(gprlist_read0data), .gprr1(gprlist_read1data), .clock(clkout), .rdata(RData), .busavail(BusAvail),
    .rregno(rdispatch_rregno), .gpr1read(rdispatch_gpr1read), .gpr1regno(rdispatch_gpr1regno),
    .rval(rdispatch_rval), .wregno(rdispatch_wregno), .error(rdispatch_error), .wval(rdispatch_wval),
    .gprwrite(rdispatch_gprwrite), .iowrite(rdispatch_iowrite), .be(rdispatch_be), .w(W), .io(IO),
    .sc(rdispatch_sc), .addr(rdispatch_addr), .wdata(rdispatch_wdata));  // open: writeval, readregno, addrregno, ioread, writeregno, mapno, sysctlread, wb, dir, write, shift, portno, width, syswrite, shiften, swidth
  Multiplexer #(.width(5)) multiplexer_3 (
    .in1(rdispatch_wregno), .out(multiplexer_3_out), .sel(rdispatch_iowrite));  // open: in0
  Multiplexer #(.width(5)) multiplexer_4 (
    .in1(rdispatch_gpr1regno), .out(multiplexer_4_out), .sel(rdispatch_gpr1read));  // open: in0
  Multiplexer #(.width(32)) multiplexer_5 (
    .in1(rdispatch_wval), .out(multiplexer_5_out), .sel(rdispatch_iowrite));  // open: in0
endmodule

module alu (
  input  [31:0] leftin,
  input  [31:0] rightin,
  input  [4:0] shiftq,
  input  shiftp,
  input  [2:0] op,
  output [31:0] result,
  output [4:0] flags
);

  wire decoder_1_out2;
  wire [4:0] demultiplexer_1_out0, demultiplexer_1_out1;
  wire [31:0] adder_result, and_1_out, or_1_out, shifter_1_out, shifter_2_out, xor_1_out;

  Demultiplexer #(.width(5)) demultiplexer_1 (
    .out0(demultiplexer_1_out0), .out1(demultiplexer_1_out1), .in(shiftq), .sel(shiftp));
  Decoder #(.enable("false"), .select(3)) decoder_1 (
    .out2(decoder_1_out2), .sel(op));  // open: out0, out1, out3, out4, out5, out6, out7
  Shifter #(.width(32)) shifter_1 (.in(leftin), .\dist (demultiplexer_1_out0), .out(shifter_1_out));
  Shifter #(.width(32)) shifter_2 (.in(rightin), .\dist (demultiplexer_1_out1), .out(shifter_2_out));
  assign and_1_out = shifter_1_out & shifter_2_out;  // AND_Gate and_1, 32 bits wide
  assign or_1_out = shifter_1_out | shifter_2_out;  // OR_Gate or_1, 32 bits wide
  assign xor_1_out = shifter_1_out ^ shifter_2_out;  // XOR_Gate xor_1, 32 bits wide
  addunit adder (
    .v1(shifter_1_out), .sub(decoder_1_out2), .v2(shifter_2_out), .result(adder_result), .overflow(flags[0]),
    .carry(flags[1]));
  Multiplexer #(.select(3), .width(32)) multiplexer_1 (
    .in0(adder_result), .in1(adder_result), .in2(adder_result), .in3(and_1_out), .in4(or_1_out),
    .in5(xor_1_out), .in6({32{1'b0}}), .in7({32{1'b0}}), .out(result), .sel(op));
  lflags lfu (.val(result), .negative(flags[2]), .zero(flags[3]), .parity(flags[4]));
endmodule

module shiftunit (
  input  [31:0] value,
  input  wrap,
  input  [31:0] shiftq,
  input  dir,
  input  invertsign,
  input  [31:0] remainder,
  output [31:0] result,
  output [4:0] flags
);

  wire and_1_out, and_2_out, or_1_out;
  wire [31:0] bit_extender_1_out, xor_1_out;

  or or_1 (or_1_out, shiftq[5], shiftq[6], shiftq[7], shiftq[8], shiftq[9], shiftq[10], shiftq[11], shiftq[12], shiftq[13], shiftq[14], shiftq[15], shiftq[16], shiftq[17], shiftq[18], shiftq[19], shiftq[20], shiftq[21], shiftq[22], shiftq[23], shiftq[24], shiftq[25], shiftq[26], shiftq[27], shiftq[28], shiftq[29], shiftq[30], shiftq[31]);
  and and_1 (and_1_out, ~wrap, or_1_out);  // AND_Gate
  and and_2 (and_2_out, value[31], invertsign);
  assign bit_extender_1_out = {{31{and_2_out}}, and_2_out};  // Bit_Extender bit_extender_1
  assign xor_1_out = bit_extender_1_out ^ remainder;  // XOR_Gate xor_1, 32 bits wide
  bshifter barrel (
    .val(value), .shiftin(xor_1_out), .dir(dir), .overshift(and_1_out), .shiftq(shiftq[4:0]), .outval(result));  // open: shiftout
  lflags flagsunit (.val(result), .negative(flags[2]), .zero(flags[3]), .parity(flags[4]));

  assign flags[1:0] = 2'b00;
endmodule

module bshifter (
  input  [31:0] val,
  input  [31:0] shiftin,
  input  dir,
  input  overshift,
  input  [4:0] shiftq,
  output [31:0] outval,
  output [31:0] shiftout
);

  wire [2:0] shifts4_shiftout;
  wire [7:0] shifts3_shiftout;
  wire [15:0] shifts2_shiftout;
  wire [31:0] multiplexer_1_out, multiplexer_2_out, shifts1_nextshift, shifts1_outval, shifts1_shiftout,
       shifts2_nextshift, shifts2_outval, shifts3_nextshift, shifts3_outval, shifts4_nextshift,
       shifts4_outval;

  Multiplexer #(.width(32)) multiplexer_1 (.in0(val), .in1(shiftin), .out(multiplexer_1_out), .sel(overshift));
  Multiplexer #(.width(32)) multiplexer_2 (
    .in0({{16{1'b0}}, shifts1_shiftout[31:16]}), .in1(shifts1_shiftout), .out(multiplexer_2_out),
    .sel(shiftq[4]));
  pshift16 shifts1 (
    .base(multiplexer_1_out), .shiftin(shiftin), .dir(dir), .en(shiftq[4]), .outval(shifts1_outval),
    .nextshift(shifts1_nextshift), .shiftout(shifts1_shiftout[15:0]));
  Multiplexer #(.width(16)) multiplexer_3 (
    .in0({{8{1'b0}}, shifts2_shiftout[15:8]}), .in1(shifts2_shiftout), .out(shifts1_shiftout[31:16]),
    .sel(shiftq[3]));
  pshift8 shifts2 (
    .base(shifts1_outval), .shiftin(shifts1_nextshift), .dir(dir), .en(shiftq[3]), .outval(shifts2_outval),
    .nextshift(shifts2_nextshift), .shiftout(shifts2_shiftout[7:0]));
  Multiplexer #(.width(8)) multiplexer_4 (
    .in0({4'b0000, shifts3_shiftout[7:4]}), .in1(shifts3_shiftout), .out(shifts2_shiftout[15:8]),
    .sel(shiftq[2]));
  pshift4 shifts3 (
    .base(shifts2_outval), .shiftin(shifts2_nextshift), .dir(dir), .en(shiftq[2]), .outval(shifts3_outval),
    .nextshift(shifts3_nextshift), .shiftout(shifts3_shiftout[3:0]));
  Multiplexer #(.width(4)) multiplexer_5 (
    .in0({3'b000, shifts4_shiftout[2]}), .in1({1'b0, shifts4_shiftout}), .out(shifts3_shiftout[7:4]),
    .sel(shiftq[1]));
  pshift2 shifts4 (
    .base(shifts3_outval), .shiftin(shifts3_nextshift), .dir(dir), .en(shiftq[1]), .outval(shifts4_outval),
    .nextshift(shifts4_nextshift), .shiftout(shifts4_shiftout[1:0]));
  pshift1 shifts5 (
    .base(shifts4_outval), .shiftin(shifts4_nextshift), .dir(dir), .en(shiftq[0]), .outval(outval),
    .shiftout(shifts4_shiftout[2]));
  Multiplexer #(.width(32)) multiplexer_6 (.in0(multiplexer_2_out), .in1(val), .out(shiftout), .sel(overshift));
endmodule

module pshift16 (
  input  [31:0] base,
  input  [31:0] shiftin,
  input  dir,
  input  en,
  output [31:0] outval,
  output [31:0] nextshift,
  output [15:0] shiftout
);

  wire [15:0] multiplexer_1_out, multiplexer_2_out;

  Multiplexer #(.width(16)) multiplexer_1 (.in0(shiftin[31:16]), .in1(base[31:16]), .out(multiplexer_1_out), .sel(dir));
  Multiplexer #(.width(16)) multiplexer_2 (.in0(base[15:0]), .in1(shiftin[15:0]), .out(multiplexer_2_out), .sel(dir));
  Multiplexer #(.width(16)) multiplexer_3 (.in0(base[15:0]), .in1(multiplexer_1_out), .out(outval[15:0]), .sel(en));
  Multiplexer #(.width(16)) multiplexer_4 (.in0(base[31:16]), .in1(multiplexer_2_out), .out(outval[31:16]), .sel(en));
  Multiplexer #(.width(16)) multiplexer_5 (.in0(shiftin[15:0]), .in1(shiftin[31:16]), .out(nextshift[15:0]), .sel(en));
  Multiplexer #(.width(16)) multiplexer_6 (.in0(shiftin[31:16]), .in1(shiftin[15:0]), .out(nextshift[31:16]), .sel(en));
  Multiplexer #(.enable("true"), .width(16)) multiplexer_7 (
    .in0(base[31:16]), .in1(base[15:0]), .out(shiftout), .sel(dir), .en(en));

  // Notes on the sheet:
  //   Bits 0-15
  //   Bits 16-31
endmodule

module pshift8 (
  input  [31:0] base,
  input  [31:0] shiftin,
  input  dir,
  input  en,
  output [31:0] outval,
  output [31:0] nextshift,
  output [7:0] shiftout
);

  wire [31:0] multiplexer_1_out, multiplexer_2_out;

  Multiplexer #(.width(32)) multiplexer_1 (
    .in0({base[23:0], shiftin[31:24]}), .in1({shiftin[7:0], base[31:8]}), .out(multiplexer_1_out), .sel(dir));
  Multiplexer #(.width(32)) multiplexer_2 (
    .in0({shiftin[23:0], shiftin[31:24]}), .in1({shiftin[7:0], shiftin[31:8]}), .out(multiplexer_2_out),
    .sel(dir));
  Multiplexer #(.enable("true"), .width(8)) multiplexer_3 (
    .in0(shiftin[7:0]), .in1(base[7:0]), .out(shiftout), .sel(dir), .en(en));
  Multiplexer #(.width(32)) multiplexer_4 (.in0(base), .in1(multiplexer_1_out), .out(outval), .sel(en));
  Multiplexer #(.width(32)) multiplexer_5 (.in0(shiftin), .in1(multiplexer_2_out), .out(nextshift), .sel(en));
endmodule

module pshift4 (
  input  [31:0] base,
  input  [31:0] shiftin,
  input  dir,
  input  en,
  output [31:0] outval,
  output [31:0] nextshift,
  output [3:0] shiftout
);

  wire [31:0] multiplexer_1_out, multiplexer_2_out;

  Multiplexer #(.width(32)) multiplexer_1 (
    .in0({base[27:0], shiftin[31:28]}), .in1({shiftin[3:0], base[31:4]}), .out(multiplexer_1_out), .sel(dir));
  Multiplexer #(.width(32)) multiplexer_2 (
    .in0({shiftin[27:0], shiftin[31:28]}), .in1({shiftin[3:0], shiftin[31:4]}), .out(multiplexer_2_out),
    .sel(dir));
  Multiplexer #(.width(32)) multiplexer_3 (.in0(base), .in1(multiplexer_1_out), .out(outval), .sel(en));
  Multiplexer #(.enable("true"), .width(4)) multiplexer_4 (
    .in0(base[31:28]), .in1(base[3:0]), .out(shiftout), .sel(dir), .en(en));
  Multiplexer #(.width(32)) multiplexer_5 (.in0(shiftin), .in1(multiplexer_2_out), .out(nextshift), .sel(en));
endmodule

module pshift2 (
  input  [31:0] base,
  input  [31:0] shiftin,
  input  dir,
  input  en,
  output [31:0] outval,
  output [31:0] nextshift,
  output [1:0] shiftout
);

  wire [31:0] multiplexer_1_out, multiplexer_2_out;

  Multiplexer #(.width(32)) multiplexer_1 (
    .in0({base[29:0], shiftin[31:30]}), .in1({shiftin[1:0], base[31:2]}), .out(multiplexer_1_out), .sel(dir));
  Multiplexer #(.width(32)) multiplexer_2 (
    .in0({shiftin[29:0], shiftin[31:30]}), .in1({shiftin[1:0], shiftin[31:2]}), .out(multiplexer_2_out),
    .sel(dir));
  Multiplexer #(.width(32)) multiplexer_3 (.in0(base), .in1(multiplexer_1_out), .out(outval), .sel(en));
  Multiplexer #(.width(32)) multiplexer_4 (.in0(shiftin), .in1(multiplexer_2_out), .out(nextshift), .sel(en));
  Multiplexer #(.enable("true"), .width(2)) multiplexer_5 (
    .in0(base[31:30]), .in1(base[1:0]), .out(shiftout), .sel(dir), .en(en));
endmodule

module pshift1 (
  input  [31:0] base,
  input  [31:0] shiftin,
  input  dir,
  input  en,
  output [31:0] outval,
  output shiftout
);

  wire [31:0] multiplexer_1_out;

  Multiplexer #(.width(32)) multiplexer_1 (
    .in0({base[30:0], shiftin[31]}), .in1({shiftin[0], base[31:1]}), .out(multiplexer_1_out), .sel(dir));
  Multiplexer #(.enable("true")) multiplexer_2 (.in0(base[31]), .in1(base[0]), .out(shiftout), .sel(dir), .en(en));
  Multiplexer #(.width(32)) multiplexer_3 (.in0(base), .in1(multiplexer_1_out), .out(outval), .sel(en));
endmodule

module lflags (
  input  [31:0] val,
  output negative,
  output zero,
  output parity
);

  xor xor_1 (parity, val[0], val[1], val[2], val[3], val[4], val[5], val[6], val[7], val[8], val[9], val[10], val[11], val[12], val[13], val[14], val[15], val[17], val[18], val[19], val[20], val[21], val[22], val[23], val[24], val[25], val[26], val[27], val[28], val[29], val[30], val[31], val[16]);
  nor nor_1 (zero, val[0], val[1], val[2], val[3], val[4], val[5], val[6], val[7], val[8], val[9], val[10], val[11], val[12], val[13], val[14], val[15], val[17], val[18], val[19], val[20], val[21], val[22], val[23], val[24], val[25], val[26], val[27], val[28], val[29], val[30], val[31], val[16]);

  assign negative = val[31];
endmodule

module instrdecode (
  input  decodeen,
  input  [31:0] iword,
  input  clock,
  output error
);

  wire chk_error, demultiplexer_1_out0, demultiplexer_1_out1, demultiplexer_1_out2, demultiplexer_1_out3,
       demultiplexer_1_out4, demultiplexer_1_out5, demultiplexer_1_out6, demultiplexer_1_out7,
       demultiplexer_1_out8, demultiplexer_1_out9, demultiplexer_1_out10, demultiplexer_1_out11,
       demultiplexer_1_out12, demultiplexer_1_out13, demultiplexer_1_out14, demultiplexer_1_out15,
       demultiplexer_1_out16, demultiplexer_1_out17, demultiplexer_1_out18, demultiplexer_1_out19,
       demultiplexer_1_out20, demultiplexer_1_out21, demultiplexer_1_out22, demultiplexer_1_out23,
       demultiplexer_1_out24, demultiplexer_1_out25, demultiplexer_1_out26, demultiplexer_1_out27,
       demultiplexer_1_out28, demultiplexer_1_out29, demultiplexer_1_out30, demultiplexer_1_out31, g0_error,
       multiplexer_1_out;
  wire [23:0] decodemasks_data;

  Demultiplexer #(.select(5)) demultiplexer_1 (
    .out0(demultiplexer_1_out0), .out1(demultiplexer_1_out1), .out2(demultiplexer_1_out2),
    .out3(demultiplexer_1_out3), .out4(demultiplexer_1_out4), .out5(demultiplexer_1_out5),
    .out6(demultiplexer_1_out6), .out7(demultiplexer_1_out7), .out8(demultiplexer_1_out8),
    .out9(demultiplexer_1_out9), .out10(demultiplexer_1_out10), .out11(demultiplexer_1_out11),
    .out12(demultiplexer_1_out12), .out13(demultiplexer_1_out13), .out14(demultiplexer_1_out14),
    .out15(demultiplexer_1_out15), .out16(demultiplexer_1_out16), .out17(demultiplexer_1_out17),
    .out18(demultiplexer_1_out18), .out19(demultiplexer_1_out19), .out20(demultiplexer_1_out20),
    .out21(demultiplexer_1_out21), .out22(demultiplexer_1_out22), .out23(demultiplexer_1_out23),
    .out24(demultiplexer_1_out24), .out25(demultiplexer_1_out25), .out26(demultiplexer_1_out26),
    .out27(demultiplexer_1_out27), .out28(demultiplexer_1_out28), .out29(demultiplexer_1_out29),
    .out30(demultiplexer_1_out30), .out31(demultiplexer_1_out31), .in(decodeen), .sel(iword[7:3]));
  Multiplexer #(.enable("true"), .select(5)) multiplexer_1 (
    .in0(g0_error), .in1(1'b0), .in6(1'b1), .in7(1'b1), .in8(1'b1), .in9(1'b1), .in10(1'b1), .in11(1'b1),
    .in12(1'b1), .in13(1'b1), .in14(1'b1), .in15(1'b1), .in16(1'b1), .in17(1'b1), .in18(1'b1), .in19(1'b1),
    .in20(1'b1), .in21(1'b1), .in22(1'b1), .in23(1'b1), .in24(1'b1), .in25(1'b1), .in26(1'b1), .in27(1'b1),
    .in28(1'b1), .in29(1'b1), .in30(1'b1), .in31(1'b1), .out(multiplexer_1_out), .sel(iword[7:3]),
    .en(decodeen));  // open: in2, in3, in4, in5
  ROM #(.dataWidth(24)) decodemasks (.addr(iword[7:0]), .data(decodemasks_data));
  group0decode g0 (
    .enabled(demultiplexer_1_out0), .minor(iword[2:0]), .clock(clock), .payload(iword[31:8]), .error(g0_error));  // open: regdone, flags, IPIn, finished, rmap, dir, dest, src, addrreg, rwrite, writeback, sz, writeval
  payloadcheck chk (.payload(iword[31:8]), .mask(decodemasks_data), .error(chk_error));
  or or_1 (error, chk_error, multiplexer_1_out);
  group1decode group1decode_1 (
    .minor(iword[2:0]), .enable(demultiplexer_1_out1), .clock(clock), .payload(iword[31:8]));  // open: src1data, src2data, src3data, aluresult, shiftresult, aluflags, shiftflags, alushiftq, alushiftpolarity, wreg, src1reg, src2reg, aluop, src3reg, leftval, rightval, remainder, wrapshift, shiftq, overshift, direction, invertsign, wval, wen, finished, flagsmask, flagsval

  // Notes on the sheet:
  //   contents of decodemasks (hex, n*v repeats v):
  //   0 ffffc0 c00c00 7ff000 7ff000 0 c0 0 0 5*c00000 20000 20000 0 ffc000 7e000 7e000 0 0 0 ffffe0 ffffe0
  //   23*0 ffffff ffffff
endmodule

module group0decode (
  input  enabled,
  input  [2:0] minor,
  input  clock,
  input  [23:0] payload,
  input  regdone,
  input  [4:0] flags,
  input  [31:0] IPIn,
  output error,
  output finished,
  output [2:0] rmap,
  output dir,
  output [4:0] dest,
  output [4:0] src,
  output [4:0] addrreg,
  output rwrite,
  output writeback,
  output [1:0] sz,
  output [31:0] writeval
);

  wire and_1_out, and_2_out, condcheck_1_succes, counter_1_carry, decoder_1_out1, decoder_1_out3,
       decoder_1_out4, decoder_1_out5, decoder_1_out6, nor_1_out, not_1_out, or_1_out, or_2_out, or_3_out;
  wire [31:0] multiplexer_5_out, zsext_result;

  Decoder #(.select(3)) decoder_1 (
    .out1(decoder_1_out1), .out2(writeback), .out3(decoder_1_out3), .out4(decoder_1_out4),
    .out5(decoder_1_out5), .out6(decoder_1_out6), .sel(minor), .en(enabled));  // open: out0, out7
  Multiplexer #(.enable("true"), .width(3)) multiplexer_1 (
    .in1(payload[20:18]), .out(rmap), .sel(writeback), .en(writeback));  // open: in0
  or or_1 (or_1_out, decoder_1_out6, writeback, decoder_1_out4, decoder_1_out5);
  or or_2 (or_2_out, writeback, decoder_1_out3);
  Counter #(.max('h3f), .ongoal("load"), .width(6)) counter_1 (
    .clr(not_1_out), .load(not_1_out), .up(not_1_out), .count(clock), .clk(clock), .D(payload[5:0]),
    .carry(counter_1_carry));  // open: Q
  not not_1 (not_1_out, decoder_1_out1);
  or or_3 (or_3_out, decoder_1_out3, decoder_1_out4);
  condcheck condcheck_1 (.flags(flags), .cc(payload[16:13]), .succes(condcheck_1_succes));
  ext16 zsext (.val(payload[23:8]), .sext(payload[5]), .result(zsext_result));
  and and_1 (and_1_out, writeback, condcheck_1_succes);
  Multiplexer #(.enable("true"), .select(3)) multiplexer_2 (
    .in0(1'b1), .in1(1'b0), .in2(1'b0), .in3(and_2_out), .in4(and_2_out), .in5(1'b0), .in6(1'b0), .in7(1'b0),
    .out(error), .sel(minor), .en(enabled));
  or or_4 (rwrite, decoder_1_out6, decoder_1_out4, and_1_out, decoder_1_out5);
  Multiplexer #(.enable("true"), .select(3)) multiplexer_3 (
    .in0(1'b0), .in1(counter_1_carry), .in2(regdone), .in3(regdone), .in4(regdone), .in5(regdone),
    .in6(regdone), .out(finished), .sel(minor), .en(enabled));  // open: in7
  and and_2 (and_2_out, nor_1_out, or_3_out);
  and and_3 (dir, writeback, payload[17]);
  Multiplexer #(.enable("true"), .width(5)) multiplexer_4 (
    .in0(payload[4:0]), .in1(payload[9:5]), .out(addrreg), .sel(decoder_1_out3), .en(or_3_out));
  Multiplexer #(.enable("true"), .width(32)) multiplexer_5 (
    .in1(IPIn), .out(multiplexer_5_out), .sel(decoder_1_out6), .en(decoder_1_out6));  // open: in0
  Multiplexer #(.enable("true"), .width(5)) multiplexer_6 (
    .in1(payload[4:0]), .out(dest), .sel(or_1_out), .en(or_1_out));  // open: in0
  Multiplexer #(.enable("true"), .width(5)) multiplexer_7 (
    .in1(payload[9:5]), .out(src), .sel(or_2_out), .en(or_2_out));  // open: in0
  Multiplexer #(.enable("true"), .width(2)) multiplexer_8 (
    .in1(payload[11:10]), .out(sz), .sel(or_3_out), .en(or_3_out));  // open: in0
  Adder #(.width(32)) adder_1 (.a(zsext_result), .b(multiplexer_5_out), .out(writeval), .cin(1'b0));  // open: cout
  nor nor_1 (nor_1_out, addrreg[4], addrreg[3], addrreg[2], addrreg[1], addrreg[0]);
endmodule

module payloadcheck (
  input  [23:0] payload,
  input  [23:0] mask,
  output error
);

  wire [23:0] and_1_out;

  assign and_1_out = payload & mask;  // AND_Gate and_1, 24 bits wide
  or or_1 (error, and_1_out[0], and_1_out[1], and_1_out[2], and_1_out[3], and_1_out[4], and_1_out[5], and_1_out[6], and_1_out[7], and_1_out[8], and_1_out[9], and_1_out[10], and_1_out[11], and_1_out[13], and_1_out[14], and_1_out[15], and_1_out[16], and_1_out[17], and_1_out[18], and_1_out[19], and_1_out[20], and_1_out[21], and_1_out[22], and_1_out[23], and_1_out[12]);
endmodule

module gprs (
  input  clock,
  input  [31:0] WData1,
  input  [4:0] read0regno,
  input  [4:0] read1regno,
  input  [4:0] wregno1,
  input  WE1,
  input  [4:0] read2regno,
  input  Reset,
  input  [31:0] WData2,
  input  [4:0] wregno2,
  input  WE2,
  output [31:0] read0data,
  output [31:0] read1data,
  output [31:0] read2data
);

  wire decoder_1_out0, decoder_1_out1, decoder_1_out2, decoder_1_out3, decoder_2_out0, decoder_2_out1,
       decoder_2_out2, decoder_2_out3;
  wire [31:0] regs0_read1, regs0_read2, regs0_read3, regs0_read4, regs0_read5, regs0_read6, regs0_read7,
       regs1_read0, regs1_read1, regs1_read2, regs1_read3, regs1_read4, regs1_read5, regs1_read6,
       regs1_read7, regs2_read0, regs2_read1, regs2_read2, regs2_read3, regs2_read4, regs2_read5,
       regs2_read6, regs2_read7, regs3_read0, regs3_read1, regs3_read2, regs3_read3, regs3_read4,
       regs3_read5, regs3_read6, regs3_read7;

  Decoder #(.select(2)) decoder_1 (
    .out0(decoder_1_out0), .out1(decoder_1_out1), .out2(decoder_1_out2), .out3(decoder_1_out3),
    .sel(wregno1[4:3]), .en(WE1));
  Decoder #(.select(2)) decoder_2 (
    .out0(decoder_2_out0), .out1(decoder_2_out1), .out2(decoder_2_out2), .out3(decoder_2_out3),
    .sel(wregno2[4:3]), .en(WE2));
  regcell8 regs0 (
    .wdata1(WData1), .wdata2(WData2), .clk(clock), .reset(Reset), .wregno1(wregno1[2:0]),
    .WE1(decoder_1_out0), .wregno2(wregno2[2:0]), .WE2(decoder_2_out0), .read1(regs0_read1),
    .read2(regs0_read2), .read3(regs0_read3), .read4(regs0_read4), .read5(regs0_read5), .read6(regs0_read6),
    .read7(regs0_read7));  // open: read0
  regcell8 regs1 (
    .wdata1(WData1), .wdata2(WData2), .clk(clock), .reset(Reset), .wregno1(wregno1[2:0]),
    .WE1(decoder_1_out1), .wregno2(wregno2[2:0]), .WE2(decoder_2_out1), .read0(regs1_read0),
    .read1(regs1_read1), .read2(regs1_read2), .read3(regs1_read3), .read4(regs1_read4), .read5(regs1_read5),
    .read6(regs1_read6), .read7(regs1_read7));
  regcell8 regs2 (
    .wdata1(WData1), .wdata2(WData2), .clk(clock), .reset(Reset), .wregno1(wregno1[2:0]),
    .WE1(decoder_1_out2), .wregno2(wregno2[2:0]), .WE2(decoder_2_out2), .read0(regs2_read0),
    .read1(regs2_read1), .read2(regs2_read2), .read3(regs2_read3), .read4(regs2_read4), .read5(regs2_read5),
    .read6(regs2_read6), .read7(regs2_read7));
  regcell8 regs3 (
    .wdata1(WData1), .wdata2(WData2), .clk(clock), .reset(Reset), .wregno1(wregno1[2:0]),
    .WE1(decoder_1_out3), .wregno2(wregno2[2:0]), .WE2(decoder_2_out3), .read0(regs3_read0),
    .read1(regs3_read1), .read2(regs3_read2), .read3(regs3_read3), .read4(regs3_read4), .read5(regs3_read5),
    .read6(regs3_read6), .read7(regs3_read7));
  Multiplexer #(.select(5), .width(32)) multiplexer_1 (
    .in0({32{1'b0}}), .in1(regs0_read1), .in2(regs0_read2), .in3(regs0_read3), .in4(regs0_read4),
    .in5(regs0_read5), .in6(regs0_read6), .in7(regs0_read7), .in8(regs1_read0), .in9(regs1_read1),
    .in10(regs1_read2), .in11(regs1_read3), .in12(regs1_read4), .in13(regs1_read5), .in14(regs1_read6),
    .in15(regs1_read7), .in16(regs2_read0), .in17(regs2_read1), .in18(regs2_read2), .in19(regs2_read3),
    .in20(regs2_read4), .in21(regs2_read5), .in22(regs2_read6), .in23(regs2_read7), .in24(regs3_read0),
    .in25(regs3_read1), .in26(regs3_read2), .in27(regs3_read3), .in28(regs3_read4), .in29(regs3_read5),
    .in30(regs3_read6), .in31(regs3_read7), .out(read0data), .sel(read0regno));
  Multiplexer #(.select(5), .width(32)) multiplexer_2 (
    .in0({32{1'b0}}), .in1(regs0_read1), .in2(regs0_read2), .in3(regs0_read3), .in4(regs0_read4),
    .in5(regs0_read5), .in6(regs0_read6), .in7(regs0_read7), .in8(regs1_read0), .in9(regs1_read1),
    .in10(regs1_read2), .in11(regs1_read3), .in12(regs1_read4), .in13(regs1_read5), .in14(regs1_read6),
    .in15(regs1_read7), .in16(regs2_read0), .in17(regs2_read1), .in18(regs2_read2), .in19(regs2_read3),
    .in20(regs2_read4), .in21(regs2_read5), .in22(regs2_read6), .in23(regs2_read7), .in24(regs3_read0),
    .in25(regs3_read1), .in26(regs3_read2), .in27(regs3_read3), .in28(regs3_read4), .in29(regs3_read5),
    .in30(regs3_read6), .in31(regs3_read7), .out(read2data), .sel(read2regno));
  Multiplexer #(.select(5), .width(32)) multiplexer_3 (
    .in0({32{1'b0}}), .in1(regs0_read1), .in2(regs0_read2), .in3(regs0_read3), .in4(regs0_read4),
    .in5(regs0_read5), .in6(regs0_read6), .in7(regs0_read7), .in8(regs1_read0), .in9(regs1_read1),
    .in10(regs1_read2), .in11(regs1_read3), .in12(regs1_read4), .in13(regs1_read5), .in14(regs1_read6),
    .in15(regs1_read7), .in16(regs2_read0), .in17(regs2_read1), .in18(regs2_read2), .in19(regs2_read3),
    .in20(regs2_read4), .in21(regs2_read5), .in22(regs2_read6), .in23(regs2_read7), .in24(regs3_read0),
    .in25(regs3_read1), .in26(regs3_read2), .in27(regs3_read3), .in28(regs3_read4), .in29(regs3_read5),
    .in30(regs3_read6), .in31(regs3_read7), .out(read1data), .sel(read1regno));
endmodule

module statusunit (
  input  [3:0] COWE,
  input  [3:0] COB,
  input  clk,
  input  HLT,
  input  STP,
  input  ISERV,
  input  RESET,
  output clockout,
  output clocken,
  output [1:0] status
);

  wire d_ff_1_q, not_2_out, or_1_out, or_2_out, s_r_ff_1_q, s_r_ff_2_q, s_r_ff_3_q, s_r_ff_4_q, s_r_ff_4_qn,
       s_r_ff_5_q, s_r_ff_6_q, s_r_ff_7_q;
  wire [3:0] not_1_out;

  assign not_1_out = ~COB;  // NOT_Gate not_1, 4 bits wide
  S_R_Flip_Flop s_r_ff_1 (.S(COWE[0]), .R(RESET), .clk(clk), .Q(s_r_ff_1_q), .reset(not_1_out[0]));  // open: Qn, preset
  S_R_Flip_Flop s_r_ff_2 (.S(HLT), .R(RESET), .clk(clk), .Q(s_r_ff_2_q), .reset(ISERV));  // open: Qn, preset
  S_R_Flip_Flop s_r_ff_3 (.S(STP), .R(RESET), .clk(clk), .Q(s_r_ff_3_q));  // open: reset, Qn, preset
  S_R_Flip_Flop s_r_ff_4 (
    .S(RESET), .R(1'b0), .clk(clk), .Q(s_r_ff_4_q), .reset(not_2_out), .Qn(s_r_ff_4_qn));  // open: preset
  not not_2 (not_2_out, RESET);
  S_R_Flip_Flop s_r_ff_5 (.S(COWE[3]), .R(RESET), .clk(clk), .Q(s_r_ff_5_q), .reset(not_1_out[3]));  // open: Qn, preset
  D_Flip_Flop d_ff_1 (.D(s_r_ff_4_q), .clk(clk), .Q(d_ff_1_q), .reset(s_r_ff_4_qn));  // open: Qn, preset
  S_R_Flip_Flop s_r_ff_6 (.S(COWE[1]), .R(RESET), .clk(clk), .Q(s_r_ff_6_q), .reset(not_1_out[1]));  // open: Qn, preset
  S_R_Flip_Flop s_r_ff_7 (.S(COWE[2]), .R(RESET), .clk(clk), .Q(s_r_ff_7_q), .reset(not_1_out[2]));  // open: Qn, preset
  or or_1 (or_1_out, s_r_ff_3_q, d_ff_1_q);
  or or_2 (or_2_out, s_r_ff_1_q, s_r_ff_6_q, s_r_ff_7_q, s_r_ff_5_q);
  Priority_Encoder #(.select(2)) priority_encoder_1 (
    .in0(1'b1), .in1(or_2_out), .in2(s_r_ff_2_q), .in3(or_1_out), .out(status), .en_in(1'b1));  // open: gs, en_out
  nor nor_1 (clocken, or_2_out, s_r_ff_2_q, or_1_out);
  and and_1 (clockout, clk, clocken);
endmodule

module ioregs (
  input  clock,
  input  reset,
  input  [4:0] readreg,
  input  [4:0] wregno,
  input  WE,
  input  SE,
  input  [31:0] writeval,
  input  [4:0] width,
  output [31:0] readval,
  output [31:0] portout
);

  wire demultiplexer_1_out0, demultiplexer_1_out1, demultiplexer_1_out2, demultiplexer_1_out3, nor_1_out,
       or_1_out;
  wire [31:0] io0_read0, io0_read1, io0_read2, io0_read3, io0_read4, io0_read5, io0_read6, io0_read7,
       io1_read0, io1_read1, io1_read2, io1_read3, io1_read4, io1_read5, io1_read6, io1_read7, io2_read0,
       io2_read1, io2_read2, io2_read3, io2_read4, io2_read5, io2_read6, io2_read7, io3_read0, io3_read1,
       io3_read2, io3_read3, io3_read4, io3_read5, io3_read6, io3_read7, iorotate_outval, multiplexer_1_out,
       multiplexer_2_out;

  Demultiplexer #(.select(2)) demultiplexer_1 (
    .out0(demultiplexer_1_out0), .out1(demultiplexer_1_out1), .out2(demultiplexer_1_out2),
    .out3(demultiplexer_1_out3), .in(or_1_out), .sel(wregno[4:3]));
  or or_1 (or_1_out, WE, SE);
  nor nor_1 (nor_1_out, width[0], width[1], width[2], width[3], width[4]);
  regcell8 io0 (
    .wdata1(multiplexer_1_out), .clk(clock), .reset(reset), .wregno1(wregno[2:0]),
    .WE1(demultiplexer_1_out0), .WE2(1'b0), .read0(io0_read0), .read1(io0_read1), .read2(io0_read2),
    .read3(io0_read3), .read4(io0_read4), .read5(io0_read5), .read6(io0_read6), .read7(io0_read7));  // open: wdata2, wregno2
  regcell8 io1 (
    .wdata1(multiplexer_1_out), .clk(clock), .reset(reset), .wregno1(wregno[2:0]),
    .WE1(demultiplexer_1_out1), .WE2(1'b0), .read0(io1_read0), .read1(io1_read1), .read2(io1_read2),
    .read3(io1_read3), .read4(io1_read4), .read5(io1_read5), .read6(io1_read6), .read7(io1_read7));  // open: wdata2, wregno2
  Multiplexer #(.width(32)) multiplexer_1 (.in0(writeval), .in1(iorotate_outval), .out(multiplexer_1_out), .sel(SE));
  Multiplexer #(.enable("true"), .select(5), .width(32)) multiplexer_2 (
    .in0(io0_read0), .in1(io0_read1), .in2(io0_read2), .in3(io0_read3), .in4(io0_read4), .in5(io0_read5),
    .in6(io0_read6), .in7(io0_read7), .in8(io1_read0), .in9(io1_read1), .in10(io1_read2), .in11(io1_read3),
    .in12(io1_read4), .in13(io1_read5), .in14(io1_read6), .in15(io1_read7), .in16(io2_read0),
    .in17(io2_read1), .in18(io2_read2), .in19(io2_read3), .in20(io2_read4), .in21(io2_read5),
    .in22(io2_read6), .in23(io2_read7), .in24(io3_read0), .in25(io3_read1), .in26(io3_read2),
    .in27(io3_read3), .in28(io3_read4), .in29(io3_read5), .in30(io3_read6), .in31(io3_read7),
    .out(multiplexer_2_out), .en(SE));  // open: sel
  bshifter iorotate (
    .val(multiplexer_2_out), .shiftin(writeval), .dir(1'b1), .overshift(nor_1_out), .shiftq(width),
    .outval(iorotate_outval), .shiftout(portout));
  regcell8 io2 (
    .wdata1(multiplexer_1_out), .clk(clock), .reset(reset), .wregno1(wregno[2:0]),
    .WE1(demultiplexer_1_out2), .WE2(1'b0), .read0(io2_read0), .read1(io2_read1), .read2(io2_read2),
    .read3(io2_read3), .read4(io2_read4), .read5(io2_read5), .read6(io2_read6), .read7(io2_read7));  // open: wdata2, wregno2
  regcell8 io3 (
    .wdata1(multiplexer_1_out), .clk(clock), .reset(reset), .wregno1(wregno[2:0]),
    .WE1(demultiplexer_1_out3), .WE2(1'b0), .read0(io3_read0), .read1(io3_read1), .read2(io3_read2),
    .read3(io3_read3), .read4(io3_read4), .read5(io3_read5), .read6(io3_read6), .read7(io3_read7));  // open: wdata2, wregno2
  Multiplexer #(.select(5), .width(32)) multiplexer_3 (
    .in0(io0_read0), .in1(io0_read1), .in2(io0_read2), .in3(io0_read3), .in4(io0_read4), .in5(io0_read5),
    .in6(io0_read6), .in7(io0_read7), .in8(io1_read0), .in9(io1_read1), .in10(io1_read2), .in11(io1_read3),
    .in12(io1_read4), .in13(io1_read5), .in14(io1_read6), .in15(io1_read7), .in16(io2_read0),
    .in17(io2_read1), .in18(io2_read2), .in19(io2_read3), .in20(io2_read4), .in21(io2_read5),
    .in22(io2_read6), .in23(io2_read7), .in24(io3_read0), .in25(io3_read1), .in26(io3_read2),
    .in27(io3_read3), .in28(io3_read4), .in29(io3_read5), .in30(io3_read6), .in31(io3_read7), .out(readval),
    .sel(readreg));
endmodule

module regcell8 (
  input  [31:0] wdata1,
  input  [31:0] wdata2,
  input  clk,
  input  reset,
  input  [2:0] wregno1,
  input  WE1,
  input  [2:0] wregno2,
  input  WE2,
  output [31:0] read0,
  output [31:0] read1,
  output [31:0] read2,
  output [31:0] read3,
  output [31:0] read4,
  output [31:0] read5,
  output [31:0] read6,
  output [31:0] read7
);

  wire decoder_1_out0, decoder_1_out1, decoder_1_out2, decoder_1_out3, decoder_1_out4, decoder_1_out5,
       decoder_1_out6, decoder_1_out7, decoder_2_out0, decoder_2_out1, decoder_2_out2, decoder_2_out3,
       decoder_2_out4, decoder_2_out5, decoder_2_out6, decoder_2_out7, or_1_out, or_2_out, or_3_out,
       or_4_out, or_5_out, or_6_out, or_7_out, or_8_out;
  wire [31:0] demultiplexer_1_out0, demultiplexer_1_out1, demultiplexer_1_out2, demultiplexer_1_out3,
       demultiplexer_1_out4, demultiplexer_1_out5, demultiplexer_1_out6, demultiplexer_1_out7,
       demultiplexer_2_out0, demultiplexer_2_out1, demultiplexer_2_out2, demultiplexer_2_out3,
       demultiplexer_2_out4, demultiplexer_2_out5, demultiplexer_2_out6, demultiplexer_2_out7,
       multiplexer_1_out, multiplexer_2_out, multiplexer_3_out, multiplexer_4_out, multiplexer_5_out,
       multiplexer_6_out, multiplexer_7_out, multiplexer_8_out;

  Demultiplexer #(.enable("true"), .select(3), .width(32)) demultiplexer_1 (
    .out0(demultiplexer_1_out0), .out1(demultiplexer_1_out1), .out2(demultiplexer_1_out2),
    .out3(demultiplexer_1_out3), .out4(demultiplexer_1_out4), .out5(demultiplexer_1_out5),
    .out6(demultiplexer_1_out6), .out7(demultiplexer_1_out7), .in(wdata1), .sel(wregno1), .en(WE1));
  Demultiplexer #(.enable("true"), .select(3), .width(32)) demultiplexer_2 (
    .out0(demultiplexer_2_out0), .out1(demultiplexer_2_out1), .out2(demultiplexer_2_out2),
    .out3(demultiplexer_2_out3), .out4(demultiplexer_2_out4), .out5(demultiplexer_2_out5),
    .out6(demultiplexer_2_out6), .out7(demultiplexer_2_out7), .in(wdata2), .sel(wregno2), .en(WE2));
  Multiplexer #(.width(32)) multiplexer_1 (
    .in0(demultiplexer_1_out0), .in1(demultiplexer_2_out0), .out(multiplexer_1_out), .sel(decoder_2_out0));
  Multiplexer #(.width(32)) multiplexer_2 (
    .in0(demultiplexer_1_out1), .in1(demultiplexer_2_out1), .out(multiplexer_2_out), .sel(decoder_2_out1));
  or or_1 (or_1_out, decoder_2_out1, decoder_1_out1);
  Multiplexer #(.width(32)) multiplexer_3 (
    .in0(demultiplexer_1_out2), .in1(demultiplexer_2_out2), .out(multiplexer_3_out), .sel(decoder_2_out2));
  or or_2 (or_2_out, decoder_2_out2, decoder_1_out2);
  Multiplexer #(.width(32)) multiplexer_4 (
    .in0(demultiplexer_1_out3), .in1(demultiplexer_2_out3), .out(multiplexer_4_out), .sel(decoder_2_out3));
  or or_3 (or_3_out, decoder_2_out3, decoder_1_out3);
  Register #(.width(32)) register_1 (.D(multiplexer_1_out), .en(or_4_out), .clk(clk), .Q(read0), .clr(reset));
  or or_4 (or_4_out, decoder_2_out0, decoder_1_out0);
  Register #(.width(32)) register_2 (.D(multiplexer_2_out), .en(or_1_out), .clk(clk), .Q(read1), .clr(reset));
  Register #(.width(32)) register_3 (.D(multiplexer_3_out), .en(or_2_out), .clk(clk), .Q(read2), .clr(reset));
  Register #(.width(32)) register_4 (.D(multiplexer_4_out), .en(or_3_out), .clk(clk), .Q(read3), .clr(reset));
  Decoder #(.select(3)) decoder_1 (
    .out0(decoder_1_out0), .out1(decoder_1_out1), .out2(decoder_1_out2), .out3(decoder_1_out3),
    .out4(decoder_1_out4), .out5(decoder_1_out5), .out6(decoder_1_out6), .out7(decoder_1_out7),
    .sel(wregno1), .en(WE1));
  Decoder #(.select(3)) decoder_2 (
    .out0(decoder_2_out0), .out1(decoder_2_out1), .out2(decoder_2_out2), .out3(decoder_2_out3),
    .out4(decoder_2_out4), .out5(decoder_2_out5), .out6(decoder_2_out6), .out7(decoder_2_out7),
    .sel(wregno2), .en(WE2));
  Register #(.width(32)) register_5 (.D(multiplexer_5_out), .en(or_5_out), .clk(clk), .Q(read4), .clr(reset));
  Multiplexer #(.width(32)) multiplexer_5 (
    .in0(demultiplexer_1_out4), .in1(demultiplexer_2_out4), .out(multiplexer_5_out), .sel(decoder_2_out4));
  or or_5 (or_5_out, decoder_2_out4, decoder_1_out4);
  Register #(.width(32)) register_6 (.D(multiplexer_6_out), .en(or_6_out), .clk(clk), .Q(read5), .clr(reset));
  Multiplexer #(.width(32)) multiplexer_6 (
    .in0(demultiplexer_1_out5), .in1(demultiplexer_2_out5), .out(multiplexer_6_out), .sel(decoder_2_out5));
  or or_6 (or_6_out, decoder_2_out5, decoder_1_out5);
  Register #(.width(32)) register_7 (.D(multiplexer_7_out), .en(or_7_out), .clk(clk), .Q(read6), .clr(reset));
  Multiplexer #(.width(32)) multiplexer_7 (
    .in0(demultiplexer_1_out6), .in1(demultiplexer_2_out6), .out(multiplexer_7_out), .sel(decoder_2_out6));
  or or_7 (or_7_out, decoder_2_out6, decoder_1_out6);
  Register #(.width(32)) register_8 (.D(multiplexer_8_out), .en(or_8_out), .clk(clk), .Q(read7), .clr(reset));
  Multiplexer #(.width(32)) multiplexer_8 (
    .in0(demultiplexer_1_out7), .in1(demultiplexer_2_out7), .out(multiplexer_8_out), .sel(decoder_2_out7));
  or or_8 (or_8_out, decoder_2_out7, decoder_1_out7);
endmodule

module ipctrl (
  input  nextinstr,
  input  busavail,
  input  clock,
  input  writeip,
  input  [29:0] newaddr,
  output [29:0] exceptip,
  output [31:0] ip,
  output [29:0] jmpbase
);

  wire undriven, undriven_2;
  wire [2:0] multiplexer_1_out;
  wire [29:0] fetchip_q;

  Counter #(.max('h3fffffff), .ongoal("load"), .trigger("falling"), .width(30)) fetchip (
    .clr(undriven), .load(writeip), .up(1'b1), .clk(clock), .D(newaddr), .Q(fetchip_q));  // open: count, carry
  Counter #(.max('h3fffffff), .ongoal("load"), .trigger("falling"), .width(30)) execip (
    .clr(undriven), .load(writeip), .up(1'b1), .count(nextinstr), .clk(clock), .D(newaddr), .Q(ip[31:2]));  // open: carry
  Register #(.width(30)) saveip (.D(ip[31:2]), .en(nextinstr), .clk(clock), .Q(exceptip));  // open: clr
  Multiplexer #(.width(3)) multiplexer_1 (
    .in0(ip[4:2]), .in1(fetchip_q[2:0]), .out(multiplexer_1_out), .sel(undriven_2));
  Register #(.width(3)) register_1 (.en(undriven_2), .clk(clock), .clr(writeip));  // open: D, Q
  RAM #(.addrWidth(3), .dataWidth(32), .enables("line")) fetchbuf (
    .addr(multiplexer_1_out), .we(undriven_2), .clk(clock));  // open: din, dout

  assign ip[1:0] = 2'b00;
  assign jmpbase = ip[31:2];
endmodule

module intrunit (
  input  [3:0] except,
  input  [4:0] IRQ
);

  wire decoder_1_out0, decoder_2_out0;

  Decoder #(.enable("false"), .select(4)) decoder_1 (
    .out0(decoder_1_out0), .sel(except));  // open: out1, out2, out3, out4, out5, out6, out7, out8, out9, out10, out11, out12, out13, out14, out15
  Decoder #(.enable("false"), .select(5)) decoder_2 (
    .out0(decoder_2_out0), .sel(IRQ));  // open: out1, out2, out3, out4, out5, out6, out7, out8, out9, out10, out11, out12, out13, out14, out15, out16, out17, out18, out19, out20, out21, out22, out23, out24, out25, out26, out27, out28, out29, out30, out31
endmodule

module condcheck (
  input  [4:0] flags,
  input  [3:0] cc,
  output succes
);

  wire and_1_out, multiplexer_2_out, or_1_out, or_2_out, xor_1_out;
  wire [2:0] multiplexer_1_out, not_1_out;

  or or_1 (or_1_out, flags[0], flags[3]);
  xor xor_1 (xor_1_out, ~flags[2], flags[1]);  // XOR_Gate
  Multiplexer #(.width(3)) multiplexer_1 (.in0(cc[2:0]), .in1(not_1_out), .out(multiplexer_1_out), .sel(cc[3]));
  assign not_1_out = ~cc[2:0];  // NOT_Gate not_1, 3 bits wide
  or or_2 (or_2_out, flags[3], xor_1_out);
  and and_1 (and_1_out, xor_1_out, ~flags[3]);  // AND_Gate
  Multiplexer #(.select(3)) multiplexer_2 (
    .in0(1'b0), .in1(flags[0]), .in2(flags[3]), .in3(flags[1]), .in4(or_1_out), .in5(and_1_out),
    .in6(or_2_out), .in7(flags[2]), .out(multiplexer_2_out), .sel(multiplexer_1_out));
  xor xor_2 (succes, multiplexer_2_out, cc[3]);
endmodule

module addunit (
  input  [31:0] v1,
  input  sub,
  input  [31:0] v2,
  output [31:0] result,
  output overflow,
  output carry
);

  wire prop0_cout, prop1_cout, prop2_cout, prop3_cout, prop3_cover;
  wire [31:0] and_1_out, bit_extender_1_out, or_1_out, prop0_cxor, xor_1_out, xor_2_out;

  assign bit_extender_1_out = {{31{sub}}, sub};  // Bit_Extender bit_extender_1
  assign xor_1_out = bit_extender_1_out ^ v2;  // XOR_Gate xor_1, 32 bits wide
  assign xor_2_out = v1 ^ xor_1_out;  // XOR_Gate xor_2, 32 bits wide
  assign or_1_out = v1 | xor_1_out;  // OR_Gate or_1, 32 bits wide
  assign and_1_out = v1 & xor_1_out;  // AND_Gate and_1, 32 bits wide
  dprop8 prop0 (
    .propin(or_1_out[7:0]), .cin(sub), .gen(and_1_out[7:0]), .cxor(prop0_cxor[7:0]), .cout(prop0_cout));  // open: cover
  dprop8 prop2 (
    .propin(or_1_out[23:16]), .cin(prop1_cout), .gen(and_1_out[23:16]), .cxor(prop0_cxor[23:16]),
    .cout(prop2_cout));  // open: cover
  assign result = xor_2_out ^ prop0_cxor;  // XOR_Gate xor_3, 32 bits wide
  dprop8 prop1 (
    .propin(or_1_out[15:8]), .cin(prop0_cout), .gen(and_1_out[15:8]), .cxor(prop0_cxor[15:8]),
    .cout(prop1_cout));  // open: cover
  dprop8 prop3 (
    .propin(or_1_out[31:24]), .cin(prop2_cout), .gen(and_1_out[31:24]), .cxor(prop0_cxor[31:24]),
    .\cover (prop3_cover), .cout(prop3_cout));
  xor xor_4 (overflow, prop3_cout, prop3_cover);
  xor xor_5 (carry, prop3_cout, sub);
endmodule

module dprop8 (
  input  [7:0] propin,
  input  cin,
  input  [7:0] gen,
  output [7:0] cxor,
  output \cover ,
  output cout
);

  wire [8:0] and_1_out, and_2_out, and_3_out, and_4_out, and_5_out, and_6_out, and_7_out, and_8_out,
       bit_extender_1_out, bit_extender_2_out, bit_extender_3_out, bit_extender_4_out, bit_extender_5_out,
       bit_extender_6_out, bit_extender_7_out, bit_extender_8_out;
  wire [8:1] hprop0_prop1;
  wire [8:2] hprop1_prop2;
  wire [8:3] hprop2_prop3;
  wire [8:4] hprop3_prop4;
  wire [8:5] hprop4_prop5;
  wire [8:6] hprop5_prop6;
  wire [8:7] hprop6_prop7;
  wire [8:8] or_1_out;

  assign bit_extender_1_out = {{8{cin}}, cin};  // Bit_Extender bit_extender_1
  assign bit_extender_2_out = {{8{gen[0]}}, gen[0]};  // Bit_Extender bit_extender_2
  assign bit_extender_3_out = {{8{gen[1]}}, gen[1]};  // Bit_Extender bit_extender_3
  assign bit_extender_4_out = {{8{gen[2]}}, gen[2]};  // Bit_Extender bit_extender_4
  assign bit_extender_5_out = {{8{gen[3]}}, gen[3]};  // Bit_Extender bit_extender_5
  assign bit_extender_6_out = {{8{gen[4]}}, gen[4]};  // Bit_Extender bit_extender_6
  assign bit_extender_7_out = {{8{gen[5]}}, gen[5]};  // Bit_Extender bit_extender_7
  assign bit_extender_8_out = {{8{gen[6]}}, gen[6]};  // Bit_Extender bit_extender_8
  halfprop hprop0 (
    .bit1(propin[0]), .bit2(propin[1]), .bit3(propin[2]), .bit4(propin[3]), .bit5(propin[4]),
    .bit6(propin[5]), .bit7(propin[6]), .bit8(propin[7]), .prop1(hprop0_prop1[1]), .prop2(hprop0_prop1[2]),
    .prop3(hprop0_prop1[3]), .prop4(hprop0_prop1[4]), .prop5(hprop0_prop1[5]), .prop6(hprop0_prop1[6]),
    .prop7(hprop0_prop1[7]), .prop8(hprop0_prop1[8]));
  halfprop hprop1 (
    .bit1(1'b1), .bit2(propin[1]), .bit3(propin[2]), .bit4(propin[3]), .bit5(propin[4]), .bit6(propin[5]),
    .bit7(propin[6]), .bit8(propin[7]), .prop2(hprop1_prop2[2]), .prop3(hprop1_prop2[3]),
    .prop4(hprop1_prop2[4]), .prop5(hprop1_prop2[5]), .prop6(hprop1_prop2[6]), .prop7(hprop1_prop2[7]),
    .prop8(hprop1_prop2[8]));  // open: prop1
  halfprop hprop2 (
    .bit1(1'b1), .bit2(1'b1), .bit3(propin[2]), .bit4(propin[3]), .bit5(propin[4]), .bit6(propin[5]),
    .bit7(propin[6]), .bit8(propin[7]), .prop3(hprop2_prop3[3]), .prop4(hprop2_prop3[4]),
    .prop5(hprop2_prop3[5]), .prop6(hprop2_prop3[6]), .prop7(hprop2_prop3[7]), .prop8(hprop2_prop3[8]));  // open: prop1, prop2
  halfprop hprop3 (
    .bit1(1'b1), .bit2(1'b1), .bit3(1'b1), .bit4(propin[3]), .bit5(propin[4]), .bit6(propin[5]),
    .bit7(propin[7]), .bit8(propin[7]), .prop4(hprop3_prop4[4]), .prop5(hprop3_prop4[5]),
    .prop6(hprop3_prop4[6]), .prop7(hprop3_prop4[7]), .prop8(hprop3_prop4[8]));  // open: prop1, prop2, prop3
  halfprop hprop4 (
    .bit1(1'b1), .bit2(1'b1), .bit3(1'b1), .bit4(1'b1), .bit5(propin[4]), .bit6(propin[5]), .bit7(propin[6]),
    .bit8(propin[7]), .prop5(hprop4_prop5[5]), .prop6(hprop4_prop5[6]), .prop7(hprop4_prop5[7]),
    .prop8(hprop4_prop5[8]));  // open: prop1, prop2, prop3, prop4
  halfprop hprop5 (
    .bit1(1'b1), .bit2(1'b1), .bit3(1'b1), .bit4(1'b1), .bit5(1'b1), .bit6(propin[5]), .bit7(propin[6]),
    .bit8(propin[7]), .prop6(hprop5_prop6[6]), .prop7(hprop5_prop6[7]), .prop8(hprop5_prop6[8]));  // open: prop1, prop2, prop3, prop4, prop5
  halfprop hprop6 (
    .bit1(1'b1), .bit2(1'b1), .bit3(1'b1), .bit4(1'b1), .bit5(1'b1), .bit6(1'b1), .bit7(propin[6]),
    .bit8(propin[7]), .prop7(hprop6_prop7[7]), .prop8(hprop6_prop7[8]));  // open: prop1, prop2, prop3, prop4, prop5, prop6
  assign and_1_out = {hprop0_prop1, 1'b1} & bit_extender_1_out;  // AND_Gate and_1, 9 bits wide
  assign and_2_out = {hprop1_prop2, 2'b10} & bit_extender_2_out;  // AND_Gate and_2, 9 bits wide
  assign and_3_out = {hprop2_prop3, 3'b100} & bit_extender_3_out;  // AND_Gate and_3, 9 bits wide
  assign and_4_out = {hprop3_prop4, 4'b1000} & bit_extender_4_out;  // AND_Gate and_4, 9 bits wide
  assign and_5_out = {hprop4_prop5, 5'b10000} & bit_extender_5_out;  // AND_Gate and_5, 9 bits wide
  assign and_6_out = {hprop5_prop6, 6'b100000} & bit_extender_6_out;  // AND_Gate and_6, 9 bits wide
  assign and_7_out = {hprop6_prop7, 7'b1000000} & bit_extender_7_out;  // AND_Gate and_7, 9 bits wide
  assign and_8_out = {propin[7], 8'h80} & bit_extender_8_out;  // AND_Gate and_8, 9 bits wide
  assign {or_1_out[8], \cover , cxor[6:0]} = and_1_out | and_2_out | and_3_out | and_4_out | and_5_out | and_6_out | and_7_out | and_8_out;  // OR_Gate or_1, 9 bits wide
  or or_2 (cout, or_1_out[8], gen[7]);

  assign cxor[7] = \cover ;
endmodule

module halfprop (
  input  bit1,
  input  bit2,
  input  bit3,
  input  bit4,
  input  bit5,
  input  bit6,
  input  bit7,
  input  bit8,
  output prop1,
  output prop2,
  output prop3,
  output prop4,
  output prop5,
  output prop6,
  output prop7,
  output prop8
);

  and and_1 (prop2, bit1, bit2);
  and and_2 (prop3, bit1, bit2, bit3);
  and and_3 (prop4, bit1, bit2, bit3, bit4);
  and and_4 (prop5, bit1, bit2, bit3, bit4, bit5);
  and and_5 (prop6, bit1, bit2, bit3, bit4, bit5, bit6);
  and and_6 (prop7, bit1, bit2, bit3, bit4, bit5, bit6, bit7);
  and and_7 (prop8, bit1, bit2, bit3, bit4, bit5, bit6, bit7, bit8);

  assign prop1 = bit1;
endmodule

module extender (
  input  [31:0] valin,
  input  [4:0] width,
  input  signext,
  output [31:0] valout
);

  wire bitselector_1_out;
  wire [31:0] and_2_out, and_3_out, shifter_outval;
  wire [31:31] and_1_out;

  BitSelector #(.width(33)) bitselector_1 (.in({valin, 1'b0}), .out(bitselector_1_out), .sel({1'b0, width}));
  and and_1 (and_1_out[31], bitselector_1_out, signext);
  bshifter shifter (
    .val({32{1'b1}}), .shiftin({32{1'b0}}), .dir(1'b0), .overshift(1'b0), .shiftq(width),
    .outval(shifter_outval));  // open: shiftout
  assign and_2_out = valin & ~shifter_outval;  // AND_Gate and_2, 32 bits wide
  assign and_3_out = {32{and_1_out[31]}} & shifter_outval;  // AND_Gate and_3, 32 bits wide
  assign valout = and_2_out | and_3_out;  // OR_Gate or_1, 32 bits wide
endmodule

module ext16 (
  input  [15:0] val,
  input  sext,
  output [31:0] result
);

  and and_1 (result[31], val[15], sext);

  assign result[30:0] = {{15{result[31]}}, val};
endmodule

module group1decode (
  input  [2:0] minor,
  input  enable,
  input  clock,
  input  [23:0] payload,
  input  [31:0] src1data,
  input  [31:0] src2data,
  input  [31:0] src3data,
  input  [31:0] aluresult,
  input  [31:0] shiftresult,
  input  [4:0] aluflags,
  input  [4:0] shiftflags,
  output [4:0] alushiftq,
  output alushiftpolarity,
  output [4:0] wreg,
  output [4:0] src1reg,
  output [4:0] src2reg,
  output [2:0] aluop,
  output [4:0] src3reg,
  output [31:0] leftval,
  output [31:0] rightval,
  output [31:0] remainder,
  output wrapshift,
  output [4:0] shiftq,
  output overshift,
  output direction,
  output invertsign,
  output [31:0] wval,
  output wen,
  output finished,
  output [4:0] flagsmask,
  output [4:0] flagsval
);

  wire and_1_out, and_2_out, and_3_out, decoder_1_out0, decoder_1_out1, decoder_1_out2, decoder_1_out3,
       decoder_1_out4, decoder_1_out5, decoder_1_out6, not_1_out, or_1_out, or_2_out, or_3_out;
  wire [4:0] multiplexer_3_out;
  wire [31:0] ext16_1_result, multiplexer_4_out, multiplexer_5_out;

  Decoder #(.select(3)) decoder_1 (
    .out0(decoder_1_out0), .out1(decoder_1_out1), .out2(decoder_1_out2), .out3(decoder_1_out3),
    .out4(decoder_1_out4), .out5(decoder_1_out5), .out6(decoder_1_out6), .out7(direction), .sel(minor),
    .en(enable));
  or or_1 (or_1_out, decoder_1_out6, direction);
  or or_2 (or_2_out, decoder_1_out0, decoder_1_out1, decoder_1_out2);
  Multiplexer #(.width(32)) multiplexer_1 (.in0(src2data), .in1(multiplexer_4_out), .out(rightval), .sel(or_3_out));
  or or_3 (or_3_out, decoder_1_out1, decoder_1_out2, decoder_1_out3, decoder_1_out4, decoder_1_out5);
  and and_1 (and_1_out, payload[15], or_3_out);
  and and_2 (and_2_out, payload[15], or_1_out);
  Multiplexer #(.width(5)) multiplexer_2 (.in0(payload[9:5]), .in1(payload[4:0]), .out(src1reg), .sel(decoder_1_out0));
  and and_3 (and_3_out, decoder_1_out0, payload[6]);
  or or_4 (flagsmask[4], and_3_out, and_1_out, and_2_out);
  Multiplexer #(.enable("true"), .width(5)) multiplexer_3 (
    .in0(aluflags), .in1(shiftflags), .out(multiplexer_3_out), .sel(or_1_out), .en(flagsmask[4]));
  Multiplexer #(.width(32)) multiplexer_4 (
    .in0({payload[23:8], {16{1'b0}}}), .in1(ext16_1_result), .out(multiplexer_4_out), .sel(payload[7]));
  ext16 ext16_1 (.val(payload[23:8]), .sext(payload[5]), .result(ext16_1_result));
  Multiplexer #(.width(32)) multiplexer_5 (.in0(aluresult), .in1(shiftresult), .out(multiplexer_5_out), .sel(or_1_out));
  and and_4 (flagsmask[1], or_2_out, flagsmask[4]);
  Register #(.width(5)) register_1 (.D(multiplexer_3_out), .en(flagsmask[4]), .clk(clock), .Q(flagsval));  // open: clr
  Multiplexer #(.width(5)) multiplexer_6 (.in0(payload[14:10]), .in1({5{1'b0}}), .out(src2reg), .sel(decoder_1_out0));
  Register #(.width(32)) register_2 (.D(multiplexer_5_out), .en(enable), .clk(clock), .Q(wval), .clr(not_1_out));
  D_Flip_Flop d_ff_1 (.D(enable), .clk(clock), .Q(wen), .reset(not_1_out));  // open: Qn, preset
  not not_1 (not_1_out, enable);
  Multiplexer #(.enable("true"), .width(5)) multiplexer_7 (
    .in1(payload[20:16]), .out(alushiftq), .sel(or_3_out), .en(or_3_out));  // open: in0
  Multiplexer #(.enable("true"), .width(5)) multiplexer_8 (
    .in1(payload[23:19]), .out(src3reg), .sel(or_1_out), .en(or_1_out));  // open: in0
  or or_5 (overshift, rightval[7], rightval[5], rightval[6], rightval[8], rightval[9], rightval[10], rightval[11], rightval[12], rightval[13], rightval[14], rightval[15], rightval[16], rightval[17], rightval[18], rightval[19], rightval[20], rightval[21], rightval[22], rightval[23], rightval[24], rightval[25], rightval[26], rightval[27], rightval[28], rightval[29], rightval[30], rightval[31]);
  D_Flip_Flop d_ff_2 (.D(wen), .clk(clock), .Q(finished), .reset(not_1_out));  // open: Qn, preset

  assign aluop = minor;
  assign alushiftpolarity = payload[21];
  assign {flagsmask[3:2], flagsmask[0]} = {{2{flagsmask[4]}}, flagsmask[1]};
  assign invertsign = payload[16];
  assign leftval = src1data;
  assign remainder = src3data;
  assign shiftq = rightval[4:0];
  assign wrapshift = payload[18];
  assign wreg = payload[4:0];
endmodule

module flagsunit (
  input  [4:0] flagsw,
  input  [4:0] flagsm,
  input  reset,
  input  clock,
  input  xpv,
  output [4:0] flags
);

  wire multiplexer_1_out, multiplexer_2_out, or_1_out, or_2_out, register_1_q, register_2_q;

  Register #(.trigger("falling"), .width(1)) c (.D(flagsw[0]), .en(flagsm[0]), .clk(clock), .Q(flags[0]), .clr(reset));
  Register #(.trigger("falling"), .width(1)) v (
    .D(multiplexer_1_out), .en(or_1_out), .clk(clock), .Q(flags[1]), .clr(reset));
  Multiplexer multiplexer_1 (.in0(flagsw[1]), .in1(register_1_q), .out(multiplexer_1_out), .sel(xpv));
  or or_1 (or_1_out, flagsm[1], xpv);
  Register #(.trigger("falling"), .width(1)) z (.D(flagsw[2]), .en(flagsm[2]), .clk(clock), .Q(flags[2]), .clr(reset));
  Register #(.trigger("falling"), .width(1)) n (.D(flagsw[3]), .en(flagsm[3]), .clk(clock), .Q(flags[3]), .clr(reset));
  Register #(.trigger("falling"), .width(1)) p (
    .D(multiplexer_2_out), .en(or_2_out), .clk(clock), .Q(flags[4]), .clr(reset));
  Multiplexer multiplexer_2 (.in0(flagsw[4]), .in1(register_2_q), .out(multiplexer_2_out), .sel(xpv));
  or or_2 (or_2_out, xpv, flagsm[4]);
  Register #(.width(1)) register_1 (.D(flags[4]), .en(xpv), .clk(clock), .Q(register_1_q), .clr(reset));
  Register #(.width(1)) register_2 (.D(flags[1]), .en(xpv), .clk(clock), .Q(register_2_q), .clr(reset));
endmodule

module group2decode (
  input  en,
  input  [2:0] minor,
  input  clock,
  input  [23:0] payload,
  input  [4:0] flags,
  input  [31:0] IP,
  input  [31:0] rval,
  output [31:0] ipval,
  output jumpen,
  output [4:0] rreg,
  output wenable,
  output [4:0] wreg,
  output [31:0] wval
);

  wire cc_succes, decoder_1_out0, decoder_1_out1, decoder_1_out4, decoder_1_out5, not_1_out, or_2_out;
  wire [31:0] adder_result, bit_extender_1_out, multiplexer_1_out;

  Decoder #(.select(3)) decoder_1 (
    .out0(decoder_1_out0), .out1(decoder_1_out1), .out4(decoder_1_out4), .out5(decoder_1_out5), .sel(minor),
    .en(en));  // open: out2, out3, out6, out7
  // OR_Gate or_1 has open pins: in0=decoder_1_out4, in1=decoder_1_out5, out=open
  or or_2 (or_2_out, decoder_1_out0, decoder_1_out1);
  assign bit_extender_1_out = {{15{payload[23]}}, {payload[23:9], 2'b00}};  // Bit_Extender bit_extender_1
  condcheck cc (.flags(flags), .cc(payload[3:0]), .succes(cc_succes));
  addunit adder (.v1(bit_extender_1_out), .sub(1'b0), .v2(IP), .result(adder_result));  // open: overflow, carry
  Multiplexer #(.width(32)) multiplexer_1 (
    .in0(adder_result), .in1(rval), .out(multiplexer_1_out), .sel(decoder_1_out1));
  not not_1 (not_1_out, en);
  Register #(.width(32)) register_1 (.D(IP), .en(cc_succes), .clk(clock), .Q(wval), .clr(not_1_out));
  Register #(.width(32)) register_2 (.D(multiplexer_1_out), .en(cc_succes), .clk(clock), .Q(ipval), .clr(not_1_out));
  and and_1 (jumpen, or_2_out, cc_succes);

  assign rreg = payload[13:9];
  assign wenable = jumpen;
  assign wreg = payload[8:4];
endmodule

module sysregs (
  input  [4:0] regno,
  input  [31:0] wval,
  input  writeen
);

  ROM #(.addrWidth(5), .dataWidth(32)) writable (.addr(regno));  // open: data

  // Notes on the sheet:
  //   contents of writable (hex, n*v repeats v):
  //   80000001 0 fffffff8 28*0 ffffffff
endmodule

module coprocessordecode (
  input  [2:0] coproc,
  input  noblock,
  input  extfunc,
  input  [23:0] payload
);

  Multiplexer #(.width(32)) multiplexer_1 (
    .in0({payload[23:4], {8{1'b0}}, payload[3:0]}), .in1({payload[23:6], {8{1'b0}}, payload[5:0]}),
    .sel(extfunc));  // open: out
endmodule

module csel (
  input  [31:0] a,
  input  [31:0] b,
  input  [31:0] sel,
  output [31:0] val
);

  wire [31:0] and_1_out, and_2_out;

  assign and_1_out = a & sel;  // AND_Gate and_1, 32 bits wide
  assign and_2_out = b & ~sel;  // AND_Gate and_2, 32 bits wide
  assign val = and_1_out | and_2_out;  // OR_Gate or_1, 32 bits wide
endmodule
